// Logisim project 6.7_1.circ as structural Verilog: 1 circuit, main circuit main
module main (
  input  in_1,
  input  in_2,
  output out_3
);

  wire and_1_out, clock_1_out, j_k_ff_1_q, j_k_ff_2_q, not_1_out;

  Clock clock_1 (.out(clock_1_out));
  not not_1 (not_1_out, in_2);
  J_K_Flip_Flop j_k_ff_1 (
    .J(in_1), .clk(clock_1_out), .K(in_1), .Q(j_k_ff_1_q), .en(not_1_out));  // open: Qn, preset, reset
  and and_1 (and_1_out, j_k_ff_1_q, j_k_ff_2_q);
  J_K_Flip_Flop j_k_ff_2 (
    .J(j_k_ff_1_q), .clk(clock_1_out), .K(j_k_ff_1_q), .Q(j_k_ff_2_q), .en(not_1_out));  // open: Qn, preset, reset
  J_K_Flip_Flop j_k_ff_3 (
    .J(and_1_out), .clk(clock_1_out), .K(and_1_out), .Q(out_3), .en(not_1_out));  // open: Qn, preset, reset
endmodule
